# Fritzing sketch RFID Desk Lamp (saved by Fritzing 0.9.3b)
breadboards: 3

parts:
  Part1 = Arduino Nano (Rev3.0) (ICSP)
  U1 = 2-Channel 5v Relay Shield [package=relay-2ch5v10a]
  Part2 = RFID-RC522-v2
  U2 = POT [package=pot_alpha_rv16af-20]
  U3 = POT [package=pot_alpha_rv16af-20]
  U4 = POT [package=pot_alpha_rv16af-20]
  LED1 = RGB LED (com. cathode, rgb) [package="5 mm [THT]"]
  LED2 = smd LED [color="Red (633nm)" package="0603 [SMD]"]
  R1 = Resistor [tolerance=±5% resistance=220 package="0805 [SMD]"]
  R3 = Resistor [tolerance=±5% resistance=220 package="0805 [SMD]"]
  R4 = Resistor [tolerance=±5% resistance=220 package="0805 [SMD]"]
  R5 = Resistor [tolerance=±5% resistance=220 package="0805 [SMD]"]
  BAT1 = BC9VPC [package=bc9vpc]

nets:
  GND: Part1.GND, U1.GND, Part2.GND, U2.A, R3.Pin_0, BAT1.V-
  N1: Part1.D3, R5.Pin_0
  N2: Part1.D5, R4.Pin_0
  N3: Part1.D6, R1.Pin_0
  N4: Part1.D7, LED2.cathode
  N5: Part1.D8, U1.IN2
  N6: Part1.D9, Part2.RST
  N7: Part1.D10, Part2.SDA
  N8: Part1.D11/MOSI, Part2.MOSI
  N9: Part1.D12/MISO, Part2.MISO
  N10: Part1.VIN, BAT1.V+
  5V: Part1.5V, U1.VCC, U2.E, LED1.common_cathode
  N11: Part1.A2, U3.S
  N12: Part1.A1, U4.S
  N13: Part1.A0, U2.S
  N14: Part1.3V3, Part2.3_3V
  N15: Part1.D13/SCK, Part2.SCK
  N16: LED1.red_anode, R5.Pin_1
  N17: LED1.green_anode, R4.Pin_1
  N18: LED1.blue_anode, R1.Pin_1
  N19: LED2.anode, R3.Pin_1

custom parts:
  2-Channel 5v Relay Shield: 2 Channel 5v Relay Shield w. 2x SPD-06VDC-SD-C
  RFID-RC522-v2: A simple China made RFID-RC522 Reader; do check the pin labels, as this is a MFRC522 based clone.
